// Logisim project nand2tetris.circ as structural Verilog
module my_or (
  input  ain,
  input  bin,
  output myout
);

  wire nand_1_out, nand_2_out;

  nand nand_1 (nand_1_out, ain, ain);
  nand nand_2 (nand_2_out, bin, bin);
  nand nand_3 (myout, nand_1_out, nand_2_out);
endmodule

module my_not (
  input  myin,
  output myout
);

  nand nand_1 (myout, myin, myin);
endmodule

module my_and (
  input  a,
  input  b,
  output MyOut
);

  wire nand_1_out, nand_2_out;

  nand nand_1 (nand_1_out, a, b);
  nand nand_2 (nand_2_out, a, b);
  nand nand_3 (MyOut, nand_1_out, nand_2_out);
endmodule

module my_XOR (
  input  a,
  input  b,
  output MyOut
);

  wire and_1_out, and_2_out, not_1_out, not_2_out;

  not not_1 (not_1_out, a);
  not not_2 (not_2_out, b);
  and and_1 (and_1_out, not_1_out, b);
  and and_2 (and_2_out, a, not_2_out);
  or or_1 (MyOut, and_1_out, and_2_out);
endmodule
